# Fritzing sketch Cloud_cloud (saved by Fritzing 0.9.0b)
breadboards: 1

parts:
  Part1 = Arduino Pro Mini v13
  Part2 = HUZZAH ESP8266 Breakout
  JACK1 = 2.1mm Barrel Jack with Terminal Block
  R1 = Resistor [tolerance=±5% resistance=470 package=THT]
  C2 = Electrolytic Capacitor [capacitance=1000µF voltage=10V package="100 mil [THT, electrolytic]"]
  NEOPIXEL1 = Neopixel Strip -- White (30/m)

nets:
  N1: Part1.DTR, Part1.D0/TX, Part1.D1/RX
  N2: Part1.RAW, JACK1.POS, R1.Pin_0, C2.-, NEOPIXEL1.Din, NEOPIXEL1.+5V
  N3: Part2.RXD_5V, Part2.TXD
  N4: JACK1.NEG, C2.+, NEOPIXEL1.GND

custom parts:
  HUZZAH ESP8266 Breakout: The ESP8266 processor from Espressif is an 80 MHz microcontroller with a full WiFi front-end (both as client and access point) and TCP/IP stack with DNS support as well.
  Neopixel Strip -- White (30/m): These NeoPixel strips have 30 digitally-addressable pixel LEDs per meter and are very affordable and are only 12.5 mm wide, 10 mm if you remove the strip from the casing.
